# Fritzing sketch FritzingSketch (saved by Fritzing 0.9.3b)
breadboards: 1

parts:
  Part1 = Arduino Nano (Rev3.0)
  R1 = Resistor [tolerance=±5% resistance=330 package=THT]  # not connected
  C1 = Electrolytic Capacitor [capacitance=1mF voltage=16V package="100 mil [THT, electrolytic]"]
  NEOPIXEL3 = Neopixel Strip -- Black (30/m)
  VCC1 = 4 x AAA Battery Mount

nets:
  VIN: Part1.VIN, C1.+, NEOPIXEL3.+5V, VCC1.+
  GND: Part1.GND, C1.-, NEOPIXEL3.GND, VCC1.-

custom parts:
  Neopixel Strip -- Black (30/m): These NeoPixel strips have 30 digitally-addressable pixel LEDs per meter and are very affordable and are only 12.5 mm wide, 10 mm if you remove the strip from the casing.
